# Fritzing sketch Home Automation Diagram (saved by Fritzing 0.9.3b)

parts:
  Part1 = Arduino Uno (Rev3) - ICSP
  GLCD_128x1 = 128 x 64 Graphic LCD
  8_Channel_Relay1 = 8 Channel Power Relay
  VCC1 = Battery
  R2 = Trimmer Potentiometer [maximum_resistance=10kΩ package=THT]
  GSM_SIM_GPSR_SMS_SIM900_SIM5 = SIM800L [package=THT]

nets:
  N1: Part1.A0, 8_Channel_Relay1.IN7
  N2: Part1.A1, Part1.5V, GLCD_128x1.2_Vdd, GLCD_128x1.19_A(+), 8_Channel_Relay1.IN8, 8_Channel_Relay1.VCC#17
  N3: Part1.A3, 8_Channel_Relay1.IN6
  N4: Part1.ICSP_MOSI, Part1.D11_PWM/MOSI, GLCD_128x1.6_Enable
  N5: Part1.D8, 8_Channel_Relay1.IN3
  N6: Part1.D9_PWM, 8_Channel_Relay1.IN4
  N7: Part1.D10_PWM/SS, 8_Channel_Relay1.IN5
  N8: Part1.D12/MISO, GLCD_128x1.4_D/I
  N9: Part1.D0/RX, GSM_SIM_GPSR_SMS_SIM900_SIM5.SIM_TXD
  N10: Part1.D1/TX, GSM_SIM_GPSR_SMS_SIM900_SIM5.SIM_RXD
  N11: Part1.D2, GLCD_128x1.14_DB7
  N12: Part1.D3_PWM, GLCD_128x1.13_DB6
  N13: Part1.D4, GLCD_128x1.12_DB5
  N14: Part1.D5_PWM, GLCD_128x1.11_DB4
  N15: Part1.D6_PWM, 8_Channel_Relay1.IN1
  N16: Part1.D7, 8_Channel_Relay1.IN2
  N17: Part1.GND, GLCD_128x1.1_Vss, GLCD_128x1.20_K(-), 8_Channel_Relay1.GND#8
  N18: GLCD_128x1.3_Vo, R2.wiper
  N19: 8_Channel_Relay1.VCC#19, 8_Channel_Relay1.JD-VCC
  N20: VCC1.-, GSM_SIM_GPSR_SMS_SIM900_SIM5.GND#1
  N21: VCC1.+, GSM_SIM_GPSR_SMS_SIM900_SIM5.5V

custom parts:
  8 Channel Power Relay: An 8 channel power relay. The module operates at 5V.
